// Logisim project lab3.1.circ as structural Verilog: 1 circuit, main circuit CNTR4U
module CNTR4U (
  input  CLK,
  input  LD,
  input  CLR,
  input  D0,
  input  D1,
  input  D2,
  input  D3,
  input  ENP,
  input  ENT,
  output Q0,
  output Q1,
  output Q2,
  output Q3,
  output RCO
);

  D_Flip_Flop #(.trigger("falling")) d_ff_1 (.Q(Q0));  // open: clk, D, Qn, preset, reset
  D_Flip_Flop #(.trigger("falling")) d_ff_2 (.Q(Q1));  // open: clk, D, Qn, preset, reset
  D_Flip_Flop #(.trigger("falling")) d_ff_3 (.Q(Q2));  // open: clk, D, Qn, preset, reset
  D_Flip_Flop #(.trigger("falling")) d_ff_4 (.Q(Q3));  // open: clk, D, Qn, preset, reset

  // Notes on the sheet:
  //   输入引脚
  //   请勿修改引脚名称、电路名称及电路封装外观
  //   提示：使用独立逻辑门实现4位二进制同步计数器，禁止直接使用计数器组件。
  //   输出引脚
endmodule
