// Logisim project ec2.circ as structural Verilog: 1 circuit, main circuit main
module main (
  input  in_1,
  input  [31:0] in_2,
  input  [31:0] in_3,
  input  [31:0] in_4,
  input  [31:0] in_5,
  output out_6,
  output [31:0] out_7,
  output [31:0] out_8
);

  wire main_2_c16, main_3_c16, main_4_c16;

  lab4_2_main main_1 (
    .X(in_3[31:16]), .Y(in_5[31:16]), .C0(main_2_c16), .S(out_8[31:16]), .C16(out_6));  // open: Pg, Gg
  lab4_2_main main_2 (
    .X(in_3[15:0]), .Y(in_5[15:0]), .C0(main_3_c16), .S(out_8[15:0]), .C16(main_2_c16));  // open: Pg, Gg
  lab4_2_main main_3 (
    .X(in_2[31:16]), .Y(in_4[31:16]), .C0(main_4_c16), .S(out_7[31:16]), .C16(main_3_c16));  // open: Pg, Gg
  lab4_2_main main_4 (.X(in_2[15:0]), .Y(in_4[15:0]), .C0(in_1), .S(out_7[15:0]), .C16(main_4_c16));  // open: Pg, Gg

  // Other names for the same wires on the sheet: C0 = in_1; C64 = out_6; X_high[31:0] = in_3; X_low[31:0] = in_2;
  //   Y_high[31:0] = in_5; Y_low[31:0] = in_4; Z_high[31:0] = out_8; Z_low[31:0] = out_7
endmodule
