// Logisim project lab4.2.circ as structural Verilog: 1 circuit, main circuit main
// 16-CLA
module main (
  input  C0,
  input  [15:0] X,
  input  [15:0] Y,
  output C16,
  output Pg,
  output Gg,
  output [15:0] S
);

  wire C1, C2, C3, C4, G0, G1, G2, G3, P0, P1, P2, P3;

  lab4_1_main main_1 (.X(X[15:12]), .F(S[15:12]), .Cout(C16), .Y(Y[15:12]), .Pg(P3), .Cin(C3), .Gg(G3));
  lab4_1_main main_2 (.X(X[11:8]), .F(S[11:8]), .Y(Y[11:8]), .Pg(P2), .Cin(C2), .Gg(G2));  // open: Cout
  CLU4 clu4_1 (
    .P0(P0), .P1(P1), .P2(P2), .P3(P3), .C1(C1), .C3(C3), .G0(G0), .G1(G1), .G2(G2), .G3(G3), .C2(C2),
    .C4(C4), .C0(C0), .Pg(Pg), .Gg(Gg));
  lab4_1_main main_3 (.X(X[7:4]), .F(S[7:4]), .Y(Y[7:4]), .Pg(P1), .Cin(C1), .Gg(G1));  // open: Cout
  lab4_1_main main_4 (.X(X[3:0]), .F(S[3:0]), .Y(Y[3:0]), .Pg(P0), .Cin(C0), .Gg(G0));  // open: Cout
  // Probe on X
  // Probe on Y
  // Probe on S

  // Notes on the sheet:
  //   Y: pull=down
  //   X: pull=down
  //   C0: pull=down
  //   输入引脚区
  //   请勿修改引脚名称、电路名称及电路封装外观
  //   提示：使用4位先行进位加法器和CLU子电路实现16位并行加法器
  //   功能说明:16位Adder  S=X+Y，C16为最高位进位位，C0为进位输入， Pg、Gg为成组进位生成传递函数
  //   输出引脚区
  //   +
  //   =
  //   无符号加法
endmodule
