// Logisim project lab5.5.circ as structural Verilog: 15 circuits, main circuit main
module main (
  input  [2:0] ExtOp,
  input  [2:0] MemOp,
  input  RegWr,
  input  ALUASrc,
  input  MemWr,
  input  [1:0] ALUBSrc,
  input  [31:0] Initial_Address,
  input  [3:0] ALUctr,
  input  MemtoReg,
  input  [2:0] BandJ,
  input  clk,
  input  ReSet,
  output [31:0] PC,
  output [31:0] BusW,
  output [31:0] Din,
  output NPCASrc,
  output NPCBSrc
);


  // Other names for the same wires on the sheet: Init_Addr[31:0] = Initial_Address

  // Notes on the sheet:
  //   ALUBSrc: pull=down
  //   NPCASrc: pull=down
  //   NPCBSrc: pull=down
  //   BandJ: pull=down
  //   RegWr: pull=down
  //   ExtOp: pull=down
  //   ALUASrc: pull=down
  //   ALUctr: pull=down
  //   输入信号
  //   请勿修改引脚名称、电路名称及电路封装外观
  //   为了后续实验中的引用，不要修改控制信号的编码定义、引脚名称和在布局中的位置。
  //   指令存储器和数据存储器数据位都是32位，指令存储器编址以字为单位，数据存储器编址以字节为单位。
  //   32位数据存储器，按字节分4片存储，可按照字节、半字和字进行存储；读取字节或半字时，支持0扩展和符号位扩展。
  //   输出信号
endmodule

module BandJ (
  input  [2:0] Branch,
  input  Zero,
  input  Result0,
  output NxtASrc,
  output NxtBSrc
);


  // Notes on the sheet:
  //   Zero: pull=down
  //   Branch: pull=down
  //   输入信号
  //   请勿修改引脚名称、电路名称及电路封装外观
  //   不要修改控制信号的编码定义、引脚名称和在布局中的位置。
  //   输出信号
endmodule

module IFU (
  input  [31:0] Initial_Address,
  input  [31:0] Imm,
  input  [31:0] BusA,
  input  CLK,
  input  Reset,
  input  NxtASrc,
  input  NxtBSrc,
  output [31:0] PC
);


  // Other names for the same wires on the sheet: Init_Addr[31:0] = Initial_Address

  // Notes on the sheet:
  //   NxtASrc: pull=down
  //   BusA: pull=down
  //   NxtBSrc: pull=down
  //   Imm: pull=down
  //   输入信号
  //   请勿修改引脚名称、电路名称及电路封装外观
  //   指令存储器256KB，数据位为32位，地址位为16位。PC寄存器数据宽度32位，片选信号高电平有效
  //   输出信号
endmodule

module IDU (
  input  [31:0] IR,
  input  [31:0] BusW,
  input  [31:0] PC,
  input  [2:0] ExtOp,
  input  RegWr,
  input  ALUASrc,
  input  [1:0] ALUBSrc,
  input  CLK,
  output [31:0] DataA,
  output [31:0] DataB,
  output [31:0] BusA,
  output [31:0] BusB,
  output [6:0] OpCode,
  output [31:0] Imm,
  output [2:0] Funct3,
  output [6:0] Funct7
);


  // Other names for the same wires on the sheet: op[6:0] = OpCode

  // Notes on the sheet:
  //   ALUBSrc: pull=down
  //   ExtOp: pull=down
  //   ALUASrc: pull=down
  //   PC: pull=down
  //   RegWr: pull=down
  //   BusW: pull=down
  //   输入信号
  //   为了后续实验中的引用，不要修改ALUASrc、ALUBSrc和EXtOP编码定义。
  //   请勿修改引脚名称、电路名称及电路封装外观
  //   输出信号
  //   修改寄存器堆电路设计，0号寄存器始终为0。
endmodule

module RegFile (
  input  [4:0] R1_num,
  input  [4:0] R2_num,
  input  [4:0] Write_Reg_num,
  input  [31:0] Din,
  input  Write_Enable,
  input  Clock,
  output [31:0] Reg1Out,
  output [31:0] Reg2Out
);


  // Other names for the same wires on the sheet: CLK = Clock; RA[4:0] = R1_num; RB[4:0] = R2_num; RDA[31:0] = Reg1Out;
  //   RDB[31:0] = Reg2Out; RW[4:0] = Write_Reg_num; WE = Write_Enable

  // Notes on the sheet:
  //   输入引脚
  //   请勿修改引脚名称、电路名称及电路封装外观
  //   提示：使用译码器、多路选择器和32位寄存器及逻辑门实现寄存器堆，禁止直接使用存储器组件。
  //   输出引脚
endmodule

module \立即数扩展器  (
  input  [31:0] Instr,
  input  [2:0] Extop,
  output [31:0] imm
);


  // Notes on the sheet:
  //   Extop: pull=down
  //   Instr: pull=down
  //   输入引脚
  //   输出引脚
endmodule

module DataRAM (
  input  CLK,
  input  CLR,
  input  WE,
  input  [2:0] MemOp,
  input  [17:0] Addr,
  input  [31:0] Din,
  output AlignErr,
  output [31:0] DataOut
);


  // Other names for the same wires on the sheet: Dout[31:0] = DataOut

  // Notes on the sheet:
  //   输入引脚
  //   请勿修改引脚名称、电路名称及电路封装外观
  //   为了后续实验中的引用，不要修改MemOp的编码定义、引脚名称和在布局中的位置。
  //   32位数据存储器，按字节分4片存储，可按照字节、半字和字进行存储；读取字节或半字时，支持0扩展和符号位扩展。
  //   输出引脚
endmodule

module ALU (
  input  [3:0] ALUctr,
  input  [31:0] A,
  input  [31:0] B,
  output Zero,
  output [31:0] S
);

  // Probe on A
  // Probe on B
  // Probe on S

  // Other names for the same wires on the sheet: Result[31:0] = S

  // Notes on the sheet:
  //   A: pull=down
  //   B: pull=down
  //   ALUctr: pull=down
  //   输入引脚
  //   请勿修改引脚名称、电路名称及电路封装外观
  //   提示：使用32位并行加法器子电路、桶形移位器、ALU控制子电路实现32位ALU
  //   功能说明:32位ALU，输入32位操作数A、B，4位控制信号ALUctr，输出32位结果Reseult和1位Zero标志位
  //   输出引脚
  //   操作数和结果
endmodule

module ALUctrl (
  input  [3:0] ALUctr,
  output SUBctr,
  output SFTctr,
  output SIGctr,
  output ALctr,
  output [2:0] OPctr
);


  // Other names for the same wires on the sheet: LRctr = SFTctr

  // Notes on the sheet:
  //   输入引脚
  //   ALU操作控制信号生成部件
  //   输出引脚
endmodule

module Adder32 (
  input  Cin,
  input  [31:0] X,
  input  [31:0] Y,
  output CF,
  output Cout,
  output OF,
  output SF,
  output [31:0] S,
  output ZF
);

  // Probe on X
  // Probe on Y
  // Probe on S

  // Notes on the sheet:
  //   Y: pull=down
  //   X: pull=down
  //   Cin: pull=down
  //   输入引脚区
  //   输出引脚区
  //   请勿修改引脚名称、电路名称及电路封装外观
  //   提示：使用16位并行加法器子电路实现32位快速加法器
  //   功能说明:32位Adder  S=X+Y，Cout为最高位进位位，Cin为进位输入， S为和，溢出OF、进位CF、零ZF、符号SF。
  //   +
  //   =
  //   无符号加法
endmodule

// 移位器
module Shifter32 (
  input  [4:0] shamt,
  input  L_R,
  input  A_L,
  input  [31:0] DataIn,
  output [31:0] DataOut
);


  // Other names for the same wires on the sheet: Arth_Logic = A_L; Din[31:0] = DataIn; Dout[31:0] = DataOut;
  //   Left_Right = L_R

  // Notes on the sheet:
  //   L/R,A/L: 00逻辑右移，01算术右移，10逻辑左移，11：循环左移
  //   输入引脚
  //   请勿修改引脚名称、电路名称及电路封装外观
  //   提示：使用多路选择器、逻辑门实现32位桶形移位器，禁止直接使用移位器组件。
  //   输出引脚
endmodule

module Adder16 (
  input  C0,
  input  [15:0] X,
  input  [15:0] Y,
  output C16,
  output Pg,
  output Gg,
  output [15:0] S
);

  // Probe on X
  // Probe on Y
  // Probe on S

  // Notes on the sheet:
  //   X: pull=down
  //   C0: pull=down
  //   Y: pull=down
  //   输入引脚区
  //   请勿修改引脚名称、电路名称及电路封装外观
  //   提示：使用4位先行进位加法器和CLU子电路实现16位并行加法器
  //   功能说明:16位Adder  S=X+Y，C16为最高位进位位，C0为进位输入， Pg、Gg为成组进位生成传递函数
  //   输出引脚区
  //   +
  //   =
  //   无符号加法
endmodule

module CLA4 (
  input  [3:0] X,
  input  [3:0] Y,
  input  Cin,
  output [3:0] F,
  output Cout,
  output Pg,
  output Gg
);

  Hex_Digit_Display hex_digit_display_1 (.value(X));  // open: dp
  Hex_Digit_Display hex_digit_display_2 (.value(Y));  // open: dp
  Hex_Digit_Display hex_digit_display_3 (.value(F));  // open: dp

  // Other names for the same wires on the sheet: Z[3:0] = F

  // Notes on the sheet:
  //   +
  //   =
  //   输出
  //   输入
  //   请勿修改引脚名称、电路名称及电路封装外观
  //   提示：使用全加器和CLU子电路实现四位先行进位加法器CLA4
endmodule

module CLU4 (
  input  P0,
  input  P1,
  input  P2,
  input  P3,
  input  G0,
  input  G1,
  input  G2,
  input  G3,
  input  C0,
  output C1,
  output C3,
  output C2,
  output C4,
  output Pg,
  output Gg
);


  // Notes on the sheet:
  //   输入引脚
  //   请勿修改引脚名称、电路名称及电路封装外观
  //   提示：使用逻辑门电路实现4位四位先行进位部件CLU，Pg、Gg为成组进位生成传递函数
  //   输出引脚
endmodule

module FA (
  input  A,
  input  B,
  input  Cin,
  output F,
  output P,
  output G
);


  // Notes on the sheet:
  //   输入引脚
  //   请勿修改引脚名称、电路名称及电路封装外观
  //   输出引脚
endmodule
